// Logisim project circuit.circ as structural Verilog: 1 circuit, main circuit main
module main (
);

  wire button_2_out, button_3_out, button_4_out, clock_1_out, clock_2_out, clock_3_out,
       data_out_2_prime_sComp__11_downto_0, data_out_2_prime_sComp__12, data_out_2_prime_sComp__15_downto_0,
       EnR1, EnR2, ENT_INST__6, ENT_INST__6_down_to_0, ENT_INST__7, multiplexer_2_out, multiplexer_3_out,
       not_3_out, Oper, RST, State_0, State_1, xor_1_out;
  wire [2:0] undriven_5;
  wire [3:0] undriven_2;
  wire [6:0] adder_2_out, adder_3_out, ENT_INST__5_downto_0, not_2_out, undriven_4, undriven_6;
  wire [11:0] adder_1_out, multiplexer_1_out, multiplexer_4_out, multiplier_1_out, R1_q, R2_q,
       subtractor_1_out, undriven, undriven_3, xor_2_out;

  Button button_1 (.out(RST));
  Button button_2 (.out(button_2_out));
  Button button_3 (.out(button_3_out));
  Button button_4 (.out(button_4_out));
  Clock clock_1 (.out(clock_1_out));
  xor xor_1 (xor_1_out, State_1, State_0);
  and and_1 (EnR1, xor_1_out, State_0);
  not not_1 (EnR2, EnR1);
  and and_2 (Oper, State_1, State_0);
  Clock clock_2 (.out(clock_2_out));
  Register #(.width(12)) R1 (.D(undriven), .en(EnR1), .Q(R1_q), .clk(clock_2_out), .clr(RST));
  Adder #(.width(12)) adder_1 (.a(R1_q), .b(R2_q), .out(adder_1_out));  // open: cin, cout
  Subtractor #(.width(12)) subtractor_1 (.a(R1_q), .b(R2_q), .out(subtractor_1_out));  // open: bin, bout
  Multiplier #(.width(12)) multiplier_1 (.a(R1_q), .b(R2_q), .out(multiplier_1_out));  // open: cin, cout
  assign xor_2_out = R1_q ^ R2_q;  // XOR_Gate xor_2, 12 bits wide
  Shifter #(.width(12)) shifter_1 (.in(R2_q), .\dist (undriven_2));  // open: out
  assign not_2_out = ~ENT_INST__5_downto_0;  // NOT_Gate not_2, 7 bits wide
  not not_3 (not_3_out, data_out_2_prime_sComp__11_downto_0);
  Multiplexer #(.select(3), .width(12), .enable("false")) multiplexer_1 (
    .in0(adder_1_out), .in1(subtractor_1_out), .in2(multiplier_1_out), .in3(xor_2_out), .in4(undriven_3),
    .out(multiplexer_1_out), .sel(undriven_5));  // open: in5, in6, in7
  Adder #(.width(7)) adder_2 (.b(undriven_4), .out(adder_2_out));  // open: a, cin, cout
  Adder #(.width(7)) adder_3 (.b(undriven_6), .out(adder_3_out));  // open: a, cin, cout
  Multiplexer #(.enable("false")) multiplexer_2 (
    .in0(ENT_INST__6_down_to_0), .out(multiplexer_2_out), .sel(ENT_INST__6));  // open: in1
  Multiplexer #(.enable("false")) multiplexer_3 (
    .in0(data_out_2_prime_sComp__15_downto_0), .out(multiplexer_3_out), .sel(data_out_2_prime_sComp__12));  // open: in1
  Multiplexer #(.width(12), .enable("false")) multiplexer_4 (
    .in1(multiplexer_1_out), .out(multiplexer_4_out), .sel(Oper));  // open: in0
  Register #(.width(12)) R2 (.D(multiplexer_4_out), .en(EnR2), .Q(R2_q), .clk(clock_3_out), .clr(RST));
  Clock clock_3 (.out(clock_3_out));
  Multiplexer #(.enable("false")) multiplexer_5 (
    .out(data_out_2_prime_sComp__15_downto_0), .sel(ENT_INST__7));  // open: in0, in1

  // Notes on the sheet:
  //   RST
  //   LoadR1
  //   Unidade de controlo
  //   LoadR2
  //   Oper
  //   Conversão de sinal-módulo para complemento para 2
  //   Conversão de complemento para 2 para sinal-módulo
  //   Datapath
endmodule
