// Logisim project diagrama de blocos.circ as structural Verilog: 1 circuit, main circuit main
module main (
);

  wire _1, a, adder_1_out, ALU_select, b, c, clock_1_out, clock_2_out, clock_3_out, clock_4_out, d, e, f, g,
       h, i, multiplexer_1_out, multiplexer_2_out, multiplexer_3_out, multiplexer_4_out, multiplexer_5_out,
       multiplier_1_cout, multiplier_1_out, multiplier_2_cout, multiplier_2_out, regA1, regA1_enable, regA2,
       regM1, regM2;
  wire [2:0] M1_1_select, M1_2_select, M2_1_select, M2_2_select;

  Multiplexer #(.select(3), .enable("false")) multiplexer_1 (
    .in1(a), .in3(h), .in5(g), .in7(i), .out(multiplexer_1_out), .sel(M1_1_select));  // open: in0, in2, in4, in6
  Multiplexer #(.enable("false")) multiplexer_2 (.in0(regA1), .in1(regM1), .out(multiplexer_2_out), .sel(ALU_select));
  Multiplexer #(.select(3), .enable("false")) multiplexer_3 (
    .in1(e), .in3(f), .in5(d), .in7(regA1), .out(multiplexer_3_out), .sel(M1_2_select));  // open: in0, in2, in4, in6
  Multiplier #(.width(1)) multiplier_1 (
    .a(multiplexer_3_out), .b(multiplexer_1_out), .out(multiplier_1_out), .cout(multiplier_1_cout));  // open: cin
  Register #(.width(1)) register_1 (.D(multiplier_1_out), .Q(regM1), .clk(clock_1_out), .clr(_1));  // open: en
  Clock clock_1 (.out(clock_1_out));
  Clock clock_2 (.out(clock_2_out));
  Adder #(.width(1)) adder_1 (.a(regM2), .b(multiplexer_2_out), .out(adder_1_out));  // open: cin, cout
  Clock clock_3 (.out(clock_3_out));
  Register #(.width(1)) register_2 (.D(adder_1_out), .Q(regA1), .clk(clock_2_out), .clr(regA1_enable));  // open: en
  Register #(.width(1)) register_3 (.D(adder_1_out), .Q(regA2), .clk(clock_3_out), .clr(_1));  // open: en
  Multiplexer #(.select(3), .enable("false")) multiplexer_4 (
    .in1(e), .in3(f), .in5(d), .in7(regA2), .out(multiplexer_4_out), .sel(M2_1_select));  // open: in0, in2, in4, in6
  Multiplexer #(.select(3), .enable("false")) multiplexer_5 (
    .in1(g), .in3(h), .in5(c), .in7(b), .out(multiplexer_5_out), .sel(M2_2_select));  // open: in0, in2, in4, in6
  Multiplier #(.width(1)) multiplier_2 (
    .a(multiplexer_5_out), .b(multiplexer_4_out), .out(multiplier_2_out), .cout(multiplier_2_cout));  // open: cin
  Clock clock_4 (.out(clock_4_out));
  Register #(.width(1)) register_4 (.D(multiplier_2_out), .Q(regM2), .clk(clock_4_out), .clr(_1));  // open: en
endmodule
