// Logisim project diagrama de blocos.circ as structural Verilog: 1 circuit, main circuit main
module main (
);

  wire _1, ALU_select, clock_1_out, clock_2_out, clock_3_out, clock_4_out, clock_5_out, clock_6_out,
       clock_7_out, clock_8_out, clock_9_out, M1, M2, multiplexer_1_out, multiplexer_2_out,
       multiplexer_3_out, multiplexer_4_out, multiplexer_5_out, multiplier_1_cout, multiplier_1_out,
       multiplier_2_cout, multiplier_2_out, multiplier_3_cout, multiplier_3_out, Out, R1, R2, R3, R4,
       R4_enable, R5, Rv1, Rv2, Rv3, Rv4, subtractor_1_out;
  wire [2:0] M1_1_select, M1_2_select, M2_1_select, M2_2_select;

  Register #(.width(1)) register_1 (.D(M1), .Q(Rv1), .clk(clock_1_out), .clr(_1));  // open: en
  Clock clock_1 (.out(clock_1_out));
  Multiplexer #(.select(3), .enable("false")) multiplexer_1 (
    .in1(Rv1), .in3(M1), .in5(Rv4), .out(multiplexer_1_out), .sel(M1_1_select));  // open: in0, in2, in4, in6, in7
  Multiplexer #(.enable("false")) multiplexer_2 (.in0(R2), .in1(R4), .out(multiplexer_2_out), .sel(ALU_select));
  Clock clock_2 (.out(clock_2_out));
  Register #(.width(1)) register_2 (.D(M2), .Q(Rv2), .clk(clock_2_out), .clr(_1));  // open: en
  Multiplexer #(.select(3), .enable("false")) multiplexer_3 (
    .in1(Rv2), .in3(R1), .in5(M2), .out(multiplexer_3_out), .sel(M1_2_select));  // open: in0, in2, in4, in6, in7
  Clock clock_3 (.out(clock_3_out));
  Subtractor #(.width(1)) subtractor_1 (.a(R3), .b(multiplexer_2_out), .out(subtractor_1_out));  // open: bin, bout
  Clock clock_4 (.out(clock_4_out));
  Clock clock_5 (.out(clock_5_out));
  Multiplier #(.width(1)) multiplier_1 (
    .a(multiplexer_3_out), .b(multiplexer_1_out), .out(multiplier_1_out), .cout(multiplier_1_cout));  // open: cin
  Register #(.width(1)) register_3 (.D(multiplier_1_out), .Q(R1), .clk(clock_6_out), .clr(_1));  // open: en
  Clock clock_6 (.out(clock_6_out));
  Register #(.width(1)) register_4 (.D(subtractor_1_out), .Q(R4), .clk(clock_3_out), .clr(R4_enable));  // open: en
  Register #(.width(1)) register_5 (.D(subtractor_1_out), .Q(R5), .clk(clock_4_out), .clr(_1));  // open: en
  Register #(.width(1)) register_6 (.D(M1), .Q(Rv3), .clk(clock_5_out), .clr(_1));  // open: en
  Register #(.width(1)) register_7 (.D(M2), .Q(Rv4), .clk(clock_7_out), .clr(_1));  // open: en
  Clock clock_7 (.out(clock_7_out));
  Multiplexer #(.select(3), .enable("false")) multiplexer_4 (
    .in1(Rv3), .in3(R5), .in5(R1), .in7(M1), .out(multiplexer_4_out), .sel(M2_1_select));  // open: in0, in2, in4, in6
  Multiplier #(.width(1)) multiplier_2 (
    .a(Rv2), .b(Rv1), .out(multiplier_2_out), .cout(multiplier_2_cout));  // open: cin
  Clock clock_8 (.out(clock_8_out));
  Adder #(.width(1)) adder_1 (.a(R3), .b(R1), .out(Out));  // open: cin, cout
  Multiplexer #(.select(3), .enable("false")) multiplexer_5 (
    .in1(Rv4), .in3(M2), .in5(R1), .out(multiplexer_5_out), .sel(M2_2_select));  // open: in0, in2, in4, in6, in7
  Register #(.width(1)) register_8 (.D(multiplier_2_out), .Q(R3), .clk(clock_8_out), .clr(_1));  // open: en
  Multiplier #(.width(1)) multiplier_3 (
    .a(multiplexer_5_out), .b(multiplexer_4_out), .out(multiplier_3_out), .cout(multiplier_3_cout));  // open: cin
  Clock clock_9 (.out(clock_9_out));
  Register #(.width(1)) register_9 (.D(multiplier_3_out), .Q(R2), .clk(clock_9_out), .clr(_1));  // open: en
endmodule
